// Logisim project aoc786201-lab04.circ as structural Verilog: 1 circuit, main circuit SC
module SC (
  input  A,
  input  B,
  input  Te,
  output S,
  output Ts
);

  wire and_1_out, and_2_out, and_3_out, xor_1_out;

  and and_1 (and_1_out, A, B);
  and and_2 (and_2_out, A, Te);
  and and_3 (and_3_out, B, Te);
  xor xor_1 (xor_1_out, A, B);
  xor xor_2 (S, xor_1_out, Te);
  or or_1 (Ts, and_1_out, and_2_out, and_3_out);
endmodule
